// Logisim project bakir_becic_23145.circ as structural Verilog: 5 circuits, main circuit CPU
module CPU (
  input  in_1,
  input  in_2
);

  wire and_1_out, clock_1_out, isjr_1_out, maincontrol_1_alusrc, maincontrol_1_beq, maincontrol_1_bne,
       maincontrol_1_extop, maincontrol_1_memread, maincontrol_1_memtoreg, maincontrol_1_memwrite,
       nextpc_1_pcsrc, or_1_out, registerfile_1_p3;
  wire [1:0] maincontrol_1_regdst;
  wire [3:0] aluctrl_1_aluop0;
  wire [4:0] multiplexer_3_out;
  wire [23:0] shifter_1_out;
  wire [25:0] mipsprogramrom_1_p1_2;
  wire [29:0] incrementer_1_p1, incrementer_1_p2, multiplexer_1_out, multiplexer_2_out, nextpc_1_out_8,
       registerfile_1_p7;
  wire [31:0] bit_extender_1_out, bit_extender_2_out, mips_alu_1_p5, mips_ram_1_p7, multiplexer_4_out,
       multiplexer_5_out, registerfile_1_p1, registerfile_1_p8;
  wire [31:26] mipsprogramrom_1_p1;
  wire [31:30] registerfile_1_p7_2;

  Multiplexer #(.width(30), .enable("false")) multiplexer_1 (
    .in0(nextpc_1_out_8), .in1(registerfile_1_p7), .out(multiplexer_1_out), .sel(isjr_1_out));
  // Probe on incrementer_1_p1
  Multiplexer #(.width(30), .enable("false")) multiplexer_2 (
    .in0(incrementer_1_p2), .in1(multiplexer_1_out), .out(multiplexer_2_out), .sel(or_1_out));
  or or_1 (or_1_out, isjr_1_out, nextpc_1_pcsrc);
  Clock clock_1 (.out(clock_1_out));
  // Probe on incrementer_1_p2
  // Incrementer incrementer_1: pin names not known; wires that end beside it: incrementer_1_p1, incrementer_1_p2, {incrementer_1_p1, 2'b00}
  Register #(.width(30), .trigger("falling")) register_1 (
    .D(multiplexer_2_out), .en(in_2), .Q(incrementer_1_p1), .clk(clock_1_out), .clr(in_1));
  ISjR isjr_1 (
    .Func5(mipsprogramrom_1_p1_2[5]), .Func4(mipsprogramrom_1_p1_2[4]), .Func3(mipsprogramrom_1_p1_2[3]),
    .Out(isjr_1_out), .Func2(mipsprogramrom_1_p1_2[2]), .Func1(mipsprogramrom_1_p1_2[1]),
    .Func0(mipsprogramrom_1_p1_2[0]), .Op5(mipsprogramrom_1_p1[31]), .Op4(mipsprogramrom_1_p1[30]),
    .Op3(mipsprogramrom_1_p1[29]), .Op2(mipsprogramrom_1_p1[28]), .Op1(mipsprogramrom_1_p1[27]),
    .Op0(mipsprogramrom_1_p1[26]));
  // MIPSProgramROM mipsprogramrom_1: pin names not known; wires that end beside it: {mipsprogramrom_1_p1, mipsprogramrom_1_p1_2}
  Multiplexer #(.select(2), .width(5), .enable("false")) multiplexer_3 (
    .in0(mipsprogramrom_1_p1_2[20:16]), .in1(mipsprogramrom_1_p1_2[15:11]), .in3({5{1'b1}}),
    .out(multiplexer_3_out), .sel(maincontrol_1_regdst));  // open: in2
  // Probe on {mipsprogramrom_1_p1, mipsprogramrom_1_p1_2}
  // RegisterFile registerfile_1: pin names not known; wires that end beside it: registerfile_1_p1, clock_1_out, registerfile_1_p3, multiplexer_3_out, mipsprogramrom_1_p1_2[25:21], mipsprogramrom_1_p1_2[20:16], {registerfile_1_p7_2, registerfile_1_p7}, registerfile_1_p8
  MainControl maincontrol_1 (
    .Op5(mipsprogramrom_1_p1[31]), .Op4(mipsprogramrom_1_p1[30]), .Op3(mipsprogramrom_1_p1[29]),
    .Op2(mipsprogramrom_1_p1[28]), .Op1(mipsprogramrom_1_p1[27]), .Op0(mipsprogramrom_1_p1[26]),
    .RegDst(maincontrol_1_regdst[0]), .RegWrite(registerfile_1_p3), .ExtOp(maincontrol_1_extop),
    .ALUSrc(maincontrol_1_alusrc), .Beq(maincontrol_1_beq), .Bne(maincontrol_1_bne),
    .J(maincontrol_1_regdst[1]), .MemRead(maincontrol_1_memread), .MemWrite(maincontrol_1_memwrite),
    .MemtoReg(maincontrol_1_memtoreg));
  and and_1 (and_1_out, mipsprogramrom_1_p1_2[15], maincontrol_1_extop);
  assign bit_extender_1_out = {{16{and_1_out}}, mipsprogramrom_1_p1_2[15:0]};  // Bit_Extender bit_extender_1
  ALUCTRL aluctrl_1 (
    .op5(mipsprogramrom_1_p1[31]), .op4(mipsprogramrom_1_p1[30]), .op3(mipsprogramrom_1_p1[29]),
    .op2(mipsprogramrom_1_p1[28]), .op1(mipsprogramrom_1_p1[27]), .op0(mipsprogramrom_1_p1[26]),
    .func5(mipsprogramrom_1_p1_2[5]), .func4(mipsprogramrom_1_p1_2[4]), .func3(mipsprogramrom_1_p1_2[3]),
    .func2(mipsprogramrom_1_p1_2[2]), .func1(mipsprogramrom_1_p1_2[1]), .func0(mipsprogramrom_1_p1_2[0]),
    .aluop3(aluctrl_1_aluop0[3]), .aluop2(aluctrl_1_aluop0[2]), .aluop1(aluctrl_1_aluop0[1]),
    .aluop0(aluctrl_1_aluop0[0]));
  Multiplexer #(.width(32), .enable("false")) multiplexer_4 (
    .in0(registerfile_1_p8), .in1(bit_extender_1_out), .out(multiplexer_4_out), .sel(maincontrol_1_alusrc));
  // Mips_ALU mips_alu_1: pin names not known; wires that end beside it: {registerfile_1_p7_2, registerfile_1_p7}, multiplexer_4_out, aluctrl_1_aluop0, mipsprogramrom_1_p1_2[10:6], mips_alu_1_p5
  NextPC nextpc_1 (
    .in_1(incrementer_1_p2), .J(maincontrol_1_regdst[1]), .bne(maincontrol_1_bne),
    .in_4({registerfile_1_p7_2, registerfile_1_p7}), .beq(multiplexer_4_out), .in_6(maincontrol_1_beq),
    .in_7(mipsprogramrom_1_p1_2), .out_8(nextpc_1_out_8), .PCsrc(nextpc_1_pcsrc));
  Shifter #(.width(24), .shift("lr")) shifter_1 (.in(mips_alu_1_p5[23:0]), .\dist (5'b00010), .out(shifter_1_out));
  // MIPS_RAM mips_ram_1: pin names not known; wires that end beside it: shifter_1_out, registerfile_1_p8, maincontrol_1_memwrite, clock_1_out, maincontrol_1_memread, in_1, mips_ram_1_p7
  Multiplexer #(.width(32), .enable("false")) multiplexer_5 (
    .in0(mips_alu_1_p5), .in1(mips_ram_1_p7), .out(multiplexer_5_out), .sel(maincontrol_1_memtoreg));
  assign bit_extender_2_out = {{2{1'b0}}, incrementer_1_p2};  // Bit_Extender bit_extender_2
  Multiplexer #(.width(32), .enable("false")) multiplexer_6 (
    .in0(multiplexer_5_out), .in1(bit_extender_2_out), .out(registerfile_1_p1), .sel(maincontrol_1_regdst[1]));
endmodule

module MainControl (
  input  Op5,
  input  Op4,
  input  Op3,
  input  Op2,
  input  Op1,
  input  Op0,
  output RegDst,
  output RegWrite,
  output ExtOp,
  output ALUSrc,
  output Beq,
  output Bne,
  output J,
  output MemRead,
  output MemWrite,
  output MemtoReg
);

  wire and_2_out, and_3_out, and_4_out, and_5_out, and_6_out, and_7_out, and_10_out, and_11_out, and_13_out,
       not_1_out, not_2_out, not_3_out, not_4_out, not_5_out, not_6_out, not_7_out, not_8_out, not_9_out,
       not_10_out, not_11_out, not_12_out, not_13_out, not_15_out, not_16_out, not_17_out, not_18_out,
       not_19_out, not_20_out, not_21_out, not_22_out, not_23_out, not_24_out, not_25_out, not_26_out,
       not_27_out, not_28_out;

  not not_1 (not_1_out, Op3);
  not not_2 (not_2_out, Op1);
  not not_3 (not_3_out, Op5);
  not not_4 (not_4_out, Op4);
  not not_5 (not_5_out, Op3);
  not not_6 (not_6_out, Op2);
  not not_7 (not_7_out, Op2);
  not not_8 (not_8_out, Op1);
  not not_9 (not_9_out, Op4);
  not not_10 (not_10_out, Op3);
  not not_11 (not_11_out, Op2);
  not not_12 (not_12_out, Op5);
  not not_13 (not_13_out, Op3);
  not not_14 (ExtOp, Op2);
  or or_1 (ALUSrc, Op1, Op3);
  not not_15 (not_15_out, Op3);
  not not_16 (not_16_out, Op0);
  not not_17 (not_17_out, Op3);
  not not_18 (not_18_out, Op1);
  not not_19 (not_19_out, Op5);
  not not_20 (not_20_out, Op4);
  not not_21 (not_21_out, Op3);
  not not_22 (not_22_out, Op2);
  not not_23 (not_23_out, Op3);
  not not_24 (not_24_out, Op0);
  not not_25 (not_25_out, Op3);
  and and_1 (MemWrite, Op5, Op3);
  not not_26 (not_26_out, Op4);
  not not_27 (not_27_out, Op3);
  not not_28 (not_28_out, Op2);
  and and_2 (and_2_out, not_1_out, not_2_out);
  and and_3 (and_3_out, not_3_out, not_4_out, not_5_out, not_6_out, Op0);
  and and_4 (and_4_out, not_7_out, not_8_out);
  and and_5 (and_5_out, not_9_out, not_10_out, not_11_out, Op0);
  and and_6 (and_6_out, not_12_out, Op3);
  and and_7 (and_7_out, Op5, not_13_out);
  and and_8 (Beq, not_15_out, Op2, not_16_out);
  and and_9 (Bne, not_17_out, not_18_out, Op0);
  and and_10 (and_10_out, not_19_out, not_20_out, not_21_out, not_22_out, Op1);
  and and_11 (and_11_out, not_23_out, Op1, not_24_out);
  and and_12 (MemRead, Op5, not_25_out);
  and and_13 (and_13_out, not_26_out, not_27_out, not_28_out, Op1, Op0);
  or or_2 (RegDst, and_2_out, and_3_out);
  or or_3 (RegWrite, and_4_out, and_5_out, and_6_out, and_7_out);
  or or_4 (J, and_10_out, and_11_out);
  or or_5 (MemtoReg, and_13_out, Op5);
endmodule

module NextPC (
  input  [29:0] in_1,
  input  J,
  input  bne,
  input  [31:0] in_4,
  input  [31:0] beq,
  input  in_6,
  input  [25:0] in_7,
  output [29:0] out_8,
  output PCsrc
);

  wire and_1_out, and_2_out, comparator_1_eq, not_1_out;
  wire [29:0] adder_1_out, bit_extender_1_out;

  assign bit_extender_1_out = {{14{1'b0}}, in_7[15:0]};  // Bit_Extender bit_extender_1
  Adder #(.width(30)) adder_1 (.a(in_1), .b(bit_extender_1_out), .out(adder_1_out));  // open: cin, cout
  Multiplexer #(.width(30), .enable("false")) multiplexer_1 (
    .in0(adder_1_out), .in1({in_1[29:26], in_7}), .out(out_8), .sel(J));
  not not_1 (not_1_out, comparator_1_eq);
  Comparator #(.width(32)) comparator_1 (.a(in_4), .b(beq), .eq(comparator_1_eq));  // open: gt, lt
  and and_1 (and_1_out, not_1_out, bne);
  and and_2 (and_2_out, comparator_1_eq, in_6);
  or or_1 (PCsrc, and_1_out, J, and_2_out);

  // Notes on the sheet:
  //   NPC
  //   Imm26
  //   BUSA
  //   BUSB
  //   OUT
endmodule

module ALUCTRL (
  input  op5,
  input  op4,
  input  op3,
  input  op2,
  input  op1,
  input  op0,
  input  func5,
  input  func4,
  input  func3,
  input  func2,
  input  func1,
  input  func0,
  output aluop3,
  output aluop2,
  output aluop1,
  output aluop0
);

  wire and_1_out, and_2_out, and_3_out, and_4_out, and_5_out, and_6_out, and_7_out, and_8_out, and_9_out,
       and_10_out, and_11_out, and_12_out, and_13_out, and_14_out, and_15_out, and_16_out, and_17_out,
       and_18_out, not_1_out, not_2_out, not_3_out, not_4_out, not_5_out, not_6_out, not_7_out, not_8_out,
       not_9_out, not_10_out, not_11_out, not_12_out, not_13_out, not_14_out, not_15_out, not_16_out,
       not_17_out, not_18_out, not_19_out, not_20_out, not_21_out, not_22_out, not_23_out, not_24_out,
       not_25_out, not_26_out, not_27_out, not_28_out, not_29_out, not_30_out;

  not not_1 (not_1_out, op5);
  not not_2 (not_2_out, op3);
  and and_1 (and_1_out, not_1_out, not_2_out, func2);
  not not_3 (not_3_out, op3);
  not not_4 (not_4_out, op1);
  and and_2 (and_2_out, not_3_out, not_4_out, func2);
  not not_5 (not_5_out, op3);
  not not_6 (not_6_out, op0);
  and and_3 (and_3_out, not_5_out, not_6_out, func2);
  and and_4 (and_4_out, op4, not_7_out, func2);
  not not_7 (not_7_out, op3);
  not not_8 (not_8_out, op3);
  not not_9 (not_9_out, op1);
  and and_5 (and_5_out, not_8_out, not_9_out, func1);
  not not_10 (not_10_out, op5);
  and and_6 (and_6_out, not_10_out, op1);
  and and_7 (and_7_out, op1, not_11_out);
  not not_11 (not_11_out, op0);
  and and_8 (and_8_out, op2, op0);
  and and_9 (and_9_out, op4, op1);
  not not_12 (not_12_out, op3);
  not not_13 (not_13_out, op3);
  not not_14 (not_14_out, func2);
  not not_15 (not_15_out, op2);
  not not_16 (not_16_out, op4);
  not not_17 (not_17_out, op2);
  not not_18 (not_18_out, op5);
  not not_19 (not_19_out, op3);
  not not_20 (not_20_out, func2);
  not not_21 (not_21_out, op3);
  not not_22 (not_22_out, op1);
  not not_23 (not_23_out, func2);
  not not_24 (not_24_out, op3);
  not not_25 (not_25_out, op0);
  not not_26 (not_26_out, func2);
  not not_27 (not_27_out, op3);
  not not_28 (not_28_out, func2);
  not not_29 (not_29_out, op3);
  not not_30 (not_30_out, func2);
  or or_1 (aluop3, and_1_out, and_2_out, and_3_out, op2, and_4_out);
  or or_2 (aluop2, and_5_out, and_6_out, and_7_out, and_8_out, and_9_out);
  and and_10 (and_10_out, not_12_out, func2, func0);
  and and_11 (and_11_out, not_13_out, func5, not_14_out);
  and and_12 (and_12_out, op3, not_15_out);
  and and_13 (and_13_out, op5, not_16_out, not_17_out, op1, op0);
  and and_14 (and_14_out, not_18_out, not_19_out, not_20_out, func0);
  and and_15 (and_15_out, not_21_out, not_22_out, not_23_out, func0);
  and and_16 (and_16_out, not_24_out, not_25_out, not_26_out, func0);
  and and_17 (and_17_out, not_27_out, op2, not_28_out, func0);
  and and_18 (and_18_out, op4, not_29_out, not_30_out, func0);
  or or_3 (aluop1, and_10_out, and_11_out, and_12_out, and_13_out);
  or or_4 (aluop0, and_14_out, and_15_out, and_16_out, and_17_out, and_18_out);
endmodule

module ISjR (
  input  Func5,
  input  Func4,
  input  Func3,
  input  Func2,
  input  Func1,
  input  Func0,
  input  Op5,
  input  Op4,
  input  Op3,
  input  Op2,
  input  Op1,
  input  Op0,
  output Out
);

  wire not_1_out, not_2_out, not_3_out, not_4_out, not_5_out, not_6_out, not_7_out, not_8_out, not_9_out,
       not_10_out, not_11_out;

  not not_1 (not_1_out, Func5);
  not not_2 (not_2_out, Func4);
  not not_3 (not_3_out, Func2);
  not not_4 (not_4_out, Func1);
  not not_5 (not_5_out, Func0);
  not not_6 (not_6_out, Op5);
  not not_7 (not_7_out, Op4);
  not not_8 (not_8_out, Op3);
  not not_9 (not_9_out, Op2);
  not not_10 (not_10_out, Op1);
  not not_11 (not_11_out, Op0);
  and and_1 (Out, not_1_out, not_2_out, Func3, not_3_out, not_4_out, not_5_out, not_6_out, not_7_out, not_8_out, not_9_out, not_10_out, not_11_out);
endmodule
