// Logisim project PROVJERA.circ as structural Verilog: 4 circuits, main circuit CPU
module CPU (
  input  in_1,
  input  in_2
);

  wire and_1_out, clock_1_out, mainctrl_1_alusrc, mainctrl_1_beq, mainctrl_1_extop, mainctrl_1_regdst,
       mainctrl_1_regwrite, nextpc_1_pcsrc, registerfile_1_p1;
  wire [3:0] aluctrl_1_aluop0;
  wire [4:0] multiplexer_2_out;
  wire [29:0] incrementer_1_p2, multiplexer_1_out, nextpc_1_out, register_1_q;
  wire [31:0] bit_extender_1_out, mipsprogramrom_1_p1, multiplexer_3_out, registerfile_1_p7,
       registerfile_1_p8;

  Multiplexer #(.width(30), .enable("false")) multiplexer_1 (
    .in0(incrementer_1_p2), .in1(nextpc_1_out), .out(multiplexer_1_out), .sel(nextpc_1_pcsrc));
  Register #(.width(30), .trigger("falling")) register_1 (
    .D(multiplexer_1_out), .en(in_1), .Q(register_1_q), .clk(clock_1_out), .clr(in_2));
  Clock clock_1 (.out(clock_1_out));
  // Probe on incrementer_1_p2
  // Incrementer incrementer_1: pin names not known; wires that end beside it: register_1_q, incrementer_1_p2, {register_1_q, 2'b00}
  // MIPSProgramROM mipsprogramrom_1: pin names not known; wires that end beside it: mipsprogramrom_1_p1
  mainctrl mainctrl_1 (
    .Op5(mipsprogramrom_1_p1[31]), .Op4(mipsprogramrom_1_p1[30]), .Op3(mipsprogramrom_1_p1[29]),
    .Op2(mipsprogramrom_1_p1[28]), .Op1(mipsprogramrom_1_p1[27]), .Op0(mipsprogramrom_1_p1[26]),
    .Regwrite(mainctrl_1_regwrite), .Regdst(mainctrl_1_regdst), .Extop(mainctrl_1_extop),
    .Alusrc(mainctrl_1_alusrc), .beq(mainctrl_1_beq));
  Multiplexer #(.width(5), .enable("false")) multiplexer_2 (
    .in0(mipsprogramrom_1_p1[15:11]), .in1(mipsprogramrom_1_p1[20:16]), .out(multiplexer_2_out),
    .sel(mainctrl_1_regdst));
  // RegisterFile registerfile_1: pin names not known; wires that end beside it: registerfile_1_p1, clock_1_out, mainctrl_1_regwrite, multiplexer_2_out, mipsprogramrom_1_p1[25:21], mipsprogramrom_1_p1[20:16], registerfile_1_p7, registerfile_1_p8
  and and_1 (and_1_out, mipsprogramrom_1_p1[15], mainctrl_1_extop);
  assign bit_extender_1_out = {{16{and_1_out}}, mipsprogramrom_1_p1[15:0]};  // Bit_Extender bit_extender_1
  Multiplexer #(.width(32), .enable("false")) multiplexer_3 (
    .in0(registerfile_1_p8), .in1(bit_extender_1_out), .out(multiplexer_3_out), .sel(mainctrl_1_alusrc));
  aluctrl aluctrl_1 (
    .op5(mipsprogramrom_1_p1[31]), .op4(mipsprogramrom_1_p1[30]), .op3(mipsprogramrom_1_p1[29]),
    .op2(mipsprogramrom_1_p1[28]), .op1(mipsprogramrom_1_p1[27]), .op0(mipsprogramrom_1_p1[26]),
    .func5(mipsprogramrom_1_p1[5]), .func4(mipsprogramrom_1_p1[4]), .func3(mipsprogramrom_1_p1[3]),
    .func2(mipsprogramrom_1_p1[2]), .func1(mipsprogramrom_1_p1[1]), .func0(mipsprogramrom_1_p1[0]),
    .Aluop3(aluctrl_1_aluop0[3]), .Aluop2(aluctrl_1_aluop0[2]), .Aluop1(aluctrl_1_aluop0[1]),
    .Aluop0(aluctrl_1_aluop0[0]));
  nextpc nextpc_1 (
    .npc(incrementer_1_p2), .beq(mainctrl_1_beq), .busa(registerfile_1_p7),
    .imm26(mipsprogramrom_1_p1[25:0]), .busb(multiplexer_3_out), .out(nextpc_1_out), .PCsrc(nextpc_1_pcsrc));
  // Mips_ALU mips_alu_1: pin names not known; wires that end beside it: registerfile_1_p7, multiplexer_3_out, aluctrl_1_aluop0, registerfile_1_p1
  // Probe on nextpc_1_out
endmodule

module mainctrl (
  input  Op5,
  input  Op4,
  input  Op3,
  input  Op2,
  input  Op1,
  input  Op0,
  output Regwrite,
  output Regdst,
  output Extop,
  output Alusrc,
  output beq
);

  wire and_1_out, and_2_out, and_3_out, and_4_out, and_5_out, and_6_out, and_7_out, not_1_out, not_2_out,
       not_4_out, not_5_out, not_6_out, not_7_out, not_8_out, not_9_out, not_10_out, not_11_out, not_12_out,
       not_13_out, not_14_out, not_15_out, not_16_out;

  not not_1 (not_1_out, Op5);
  not not_2 (not_2_out, Op4);
  not not_3 (Extop, Op1);
  not not_4 (not_4_out, Op2);
  not not_5 (not_5_out, Op2);
  not not_6 (not_6_out, Op2);
  not not_7 (not_7_out, Op5);
  not not_8 (not_8_out, Op4);
  not not_9 (not_9_out, Op1);
  not not_10 (not_10_out, Op2);
  not not_11 (not_11_out, Op2);
  not not_12 (not_12_out, Op5);
  not not_13 (not_13_out, Op4);
  not not_14 (not_14_out, Op1);
  not not_15 (not_15_out, Op0);
  not not_16 (not_16_out, Op2);
  and and_1 (and_1_out, not_1_out, not_2_out, Op3, Op0);
  and and_2 (and_2_out, not_4_out, Op0);
  and and_3 (and_3_out, not_5_out, Op1);
  and and_4 (and_4_out, Op3, not_6_out);
  and and_5 (and_5_out, not_7_out, not_8_out, Op3, not_9_out, Op0);
  and and_6 (and_6_out, Op4, not_10_out);
  and and_7 (and_7_out, Op5, not_11_out);
  and and_8 (beq, not_12_out, not_13_out, Op2, not_14_out, not_15_out);
  or or_1 (Regwrite, not_16_out, Op1, and_1_out);
  or or_2 (Alusrc, and_2_out, and_3_out, and_4_out, and_5_out, and_6_out, and_7_out);

  assign Regdst = Op2;
endmodule

module aluctrl (
  input  op5,
  input  op4,
  input  op3,
  input  op2,
  input  op1,
  input  op0,
  input  func5,
  input  func4,
  input  func3,
  input  func2,
  input  func1,
  input  func0,
  output Aluop3,
  output Aluop2,
  output Aluop1,
  output Aluop0
);

  not not_1 (Aluop2, op0);

  assign Aluop0 = 1'b0;
  assign Aluop1 = op0;
  assign Aluop3 = 1'b1;
endmodule

module nextpc (
  input  [29:0] npc,
  input  beq,
  input  [31:0] busa,
  input  [25:0] imm26,
  input  [31:0] busb,
  output [29:0] out,
  output PCsrc
);

  wire comparator_1_eq;
  wire [29:0] adder_1_out, bit_extender_1_out;

  assign bit_extender_1_out = {{14{imm26[15]}}, imm26[15:0]};  // Bit_Extender bit_extender_1
  Adder #(.width(30)) adder_1 (.a(npc), .b(bit_extender_1_out), .out(adder_1_out));  // open: cin, cout
  Comparator #(.width(32)) comparator_1 (.a(busa), .b(busb), .eq(comparator_1_eq));  // open: gt, lt
  Multiplexer #(.width(30), .enable("false")) multiplexer_1 (
    .in0({npc[29:26], imm26}), .in1(adder_1_out), .out(out), .sel(beq));
  and and_1 (PCsrc, beq, comparator_1_eq);
endmodule
